# Fritzing sketch Reader_circuit (saved by Fritzing 0.9.3b)
breadboards: 1

parts:
  LED1 = LED - 5mm [color="Green (570nm)" package="5 mm [THT]"]
  LED2 = LED - 5mm [color="Red (633nm)" package="5 mm [THT]"]
  R1 = Resistor [tolerance=±5% resistance=220 package=THT]
  R2 = Resistor [tolerance=±5% resistance=220 package=THT]
  Part1 = RFID-RC522-v2
  Pico_H1 = Raspberry Pi Pico H
  OLED_I2C1 = OLED 128x64 I2C Monochrome Display
  R3 = Resistor [tolerance=±10% resistance=1.2k package="0805 [SMD]"]
  R4 = Resistor [tolerance=±10% resistance=1.2k package="0805 [SMD]"]

nets:
  N1: LED1.cathode, Pico_H1.GP16
  N2: LED1.anode, R2.Pin_1
  N3: LED2.cathode, Pico_H1.GP21
  N4: LED2.anode, R1.Pin_0
  GND: R1.Pin_1, R2.Pin_0, Part1.SCK, Part1.GND, Part1.RST, Pico_H1.GND, OLED_I2C1.GND
  N5: Part1.SDA, Pico_H1.GP5
  N6: Part1.MOSI, Pico_H1.GP6
  N7: Part1.MISO, Pico_H1.GP4
  N8: Part1.IRQ, Pico_H1.GP20
  3.3V: Part1.3.3V, Pico_H1.3V3, OLED_I2C1.VDD, R3.Pin_0, R4.Pin_0
  N9: Pico_H1.GP1, OLED_I2C1.SCK, R3.Pin_1
  N10: Pico_H1.GP0, OLED_I2C1.SDA, R4.Pin_1

custom parts:
  RFID-RC522-v2: A simple China made RFID-RC522 Reader; do check the pin labels, as this is a MFRC522 based clone.
  Raspberry Pi Pico H: Raspberry Pi Pico H. Based around the RP2040 microcontroller the Pico H is a low cost microcontroller device bringing Raspberry Pi quality, cost, and easy of use to the microcontroller space.
